# Fritzing sketch PROTOTIPADO (FZZ) (saved by Fritzing 0.9.4)
breadboards: 1

parts:
  U1 = ESP8266 NodeMCU LoLin base
  R1 = Resistor [tolerance=±5% resistance=220 package=THT]
  R2 = Resistor [tolerance=±5% resistance=220 package=THT]
  LED1 = LED - 5mm [color="Red (633nm)" package="5 mm [THT]"]
  LED2 = LED - 5mm [color="Green (560nm)" package="5 mm [THT]"]

nets:
  N1: U1.GND1-0, U1.GND8-8, R1.Pin_0, R2.Pin_0
  N2: U1.D0-0, LED2.anode
  N3: U1.D1-0, U1.D1-3, LED1.anode
  N4: R1.Pin_1, LED2.cathode
  N5: R2.Pin_1, LED1.cathode

custom parts:
  ESP8266 NodeMCU LoLin base: ESP8266 based NodeMCU Base
