# Fritzing sketch ESQUEMÁTICO (FZZ) (saved by Fritzing 0.9.4)
breadboards: 2

parts:
  U1 = ESP8266 NodeMCU LoLin base
  R1 = Resistor [tolerance=±5% resistance=10k package=THT]
  R2 = Resistor [tolerance=±5% resistance=220 package=THT]
  R3 = Resistor [tolerance=±5% resistance=220 package=THT]
  S1 = Pushbutton [package=THT]
  S2 = Pushbutton [package="[THT]"]
  LED1 = LED - 5mm [color="Green (555nm)" package="5 mm [THT]"]
  LED2 = LED - 5mm [color="Red (633nm)" package="5 mm [THT]"]
  U2 = ESP8266 NodeMCU LoLin base
  R4 = Resistor [tolerance=±5% resistance=10k package=THT]
  R5 = Resistor [tolerance=±5% resistance=220 package=THT]
  R6 = Resistor [tolerance=±5% resistance=220 package=THT]
  LED3 = LED - 5mm [color="Green (555nm)" package="5 mm [THT]"]
  LED4 = LED - 5mm [color="Red (633nm)" package="5 mm [THT]"]

nets:
  N1: U1.D0-0, LED1.anode
  N2: U1.D1-0, U1.D1-2, LED2.anode
  N3: U1.D8-0, U1.D8-2, R1.Pin_1, S1.leg0
  N4: U1.GND3-3, U1.GND8-0, R1.Pin_0, R2.Pin_0, R3.Pin_0
  N5: U1.VUSB-0, S1.leg1
  N6: R2.Pin_1, LED1.cathode
  N7: R3.Pin_1, LED2.cathode
  N8: S2.Pin_1, S2.Pin_2, U2.D8-0, U2.D8-2, R4.Pin_1
  N9: S2.Pin_3, S2.Pin_4, U2.VUSB-0
  N10: U2.D0-0, U2.D0-3, LED3.anode
  N11: U2.D1-0, U2.D1-2, LED4.anode
  N12: U2.GND3-3, U2.GND8-0, R4.Pin_0, R5.Pin_0, R6.Pin_0
  N13: R5.Pin_1, LED3.cathode
  N14: R6.Pin_1, LED4.cathode

custom parts:
  ESP8266 NodeMCU LoLin base: ESP8266 based NodeMCU Base
