# Fritzing sketch ESQUEMÁTICO (FZZ) (saved by Fritzing 0.9.4)
breadboards: 2

parts:
  U1 = ESP8266 NodeMCU LoLin base
  R1 = Resistor [tolerance=±5% resistance=220 package=THT]
  R2 = Resistor [tolerance=±5% resistance=220 package=THT]
  R3 = Resistor [tolerance=±5% resistance=220 package=THT]
  R4 = Resistor [tolerance=±5% resistance=220 package=THT]
  LED1 = LED - 5mm [color="Red (633nm)" package="5 mm [THT]"]
  LED2 = LED - 5mm [color="Red (633nm)" package="5 mm [THT]"]
  LED3 = LED - 5mm [color="Red (633nm)" package="5 mm [THT]"]
  LED4 = LED - 5mm [color="Red (633nm)" package="5 mm [THT]"]
  R5 = Rotary Potentiometer (Small) [maximum_resistance=100kΩ package=THT]
  U2 = ESP8266 NodeMCU LoLin base
  R6 = Resistor [tolerance=±5% resistance=220 package=THT]
  R7 = Resistor [tolerance=±5% resistance=220 package=THT]
  R8 = Resistor [tolerance=±5% resistance=220 package=THT]
  R9 = Resistor [tolerance=±5% resistance=220 package=THT]
  LED5 = LED - 5mm [color="Red (633nm)" package="5 mm [THT]"]
  LED6 = LED - 5mm [color="Red (633nm)" package="5 mm [THT]"]
  LED7 = LED - 5mm [color="Red (633nm)" package="5 mm [THT]"]
  LED8 = LED - 5mm [color="Red (633nm)" package="5 mm [THT]"]
  R10 = Resistor [tolerance=±5% resistance=10k package=THT]
  R11 = Photocell (LDR) [package=THT]

nets:
  N1: U1.GND1-0, U1.GND2-1, U1.GND8-4, R1.Pin_0, R2.Pin_0, R3.Pin_0, R4.Pin_0, R5.leg1
  N2: U1.D0-0, U1.D0-3, LED1.anode
  N3: U1.D1-0, U1.D1-3, LED2.anode
  N4: U1.D2-0, U1.D2-3, LED4.anode
  N5: U1.D3-0, U1.D3-3, LED3.anode
  N6: U1.A0, R5.wiper
  N7: U1.VUSB-0, R5.leg2
  N8: R1.Pin_1, LED1.cathode
  N9: R2.Pin_1, LED2.cathode
  N10: R3.Pin_1, LED4.cathode
  N11: R4.Pin_1, LED3.cathode
  N12: U2.GND1-0, U2.GND3-2, U2.GND8-10, R6.Pin_0, R7.Pin_0, R8.Pin_0, R9.Pin_0, R11.pin_0
  N13: U2.D0-0, U2.D0-3, LED5.anode
  N14: U2.D1-0, U2.D1-3, LED8.anode
  N15: U2.D2-0, U2.D2-3, LED6.anode
  N16: U2.D3-0, U2.D3-1, U2.D3-3, LED7.anode
  N17: U2.A0, R10.Pin_1, R11.pin_1
  N18: U2.VUSB-0, R10.Pin_0
  N19: R6.Pin_1, LED5.cathode
  N20: R7.Pin_1, LED8.cathode
  N21: R8.Pin_1, LED6.cathode
  N22: R9.Pin_1, LED7.cathode

custom parts:
  ESP8266 NodeMCU LoLin base: ESP8266 based NodeMCU Base
