# Fritzing sketch ESQUEMÁTICO (FZZ) (saved by Fritzing 0.9.4)
breadboards: 3

parts:
  R1 = Resistor [tolerance=±5% resistance=220 package=THT]
  R2 = Resistor [tolerance=±5% resistance=220 package=THT]
  U1 = ESP8266 NodeMCU LoLin base
  LED1 = LED - 5mm [color="Red (633nm)" package="5 mm [THT]"]
  LED2 = LED - 5mm [color="Red (633nm)" package="5 mm [THT]"]
  U2 = ESP8266 NodeMCU LoLin base
  LED3 = RGB LED - (4 legs) [package="5 mm [THT]"]
  R3 = Resistor [tolerance=±5% resistance=220 package=THT]
  R4 = Rotary Potentiometer (Small) [maximum_resistance=100kΩ package=THT]
  R5 = Resistor [tolerance=±5% resistance=10k package=THT]
  S1 = Pushbutton [package="[THT]"]
  U3 = ESP8266 NodeMCU LoLin base
  LED4 = RGB LED - (4 legs) [package="5 mm [THT]"]
  R6 = Resistor [tolerance=±5% resistance=220 package=THT]
  R7 = Rotary Potentiometer (Small) [maximum_resistance=100kΩ package=THT]
  R8 = Resistor [tolerance=±5% resistance=10k package=THT]
  S2 = Pushbutton [package="[THT]"]

nets:
  N1: R1.Pin_0, R2.Pin_0, U1.GND3-0, U1.GND8-0
  N2: R1.Pin_1, LED1.cathode
  N3: R2.Pin_1, LED2.cathode
  N4: U1.D1-0, U1.D1-2, LED1.anode
  N5: U1.D2-0, U1.D2-2, LED2.anode
  N6: U2.D0-1, U2.D0-3, U2.D1-0, U2.D1-2, U2.D1-3, LED3.red_cathode
  N7: U2.D2-0, U2.D2-3, LED3.green_cathode
  N8: U2.D3-0, U2.D3-3, LED3.blue_cathode
  N9: U2.D8-0, U2.D8-2, U2.D8-3, R5.Pin_1, S1.Pin_3, S1.Pin_4
  N10: U2.GND3-0, U2.GND3-2, U2.GND8-0, R4.leg1, R5.Pin_0
  N11: U2.A0, R4.wiper
  N12: U2.VUSB-0, U2.VUSB-3, R3.Pin_0, R4.leg2, S1.Pin_1, S1.Pin_2
  N13: LED3.common_anode, R3.Pin_1
  N14: U3.D1-0, U3.D1-3, LED4.red_cathode
  N15: U3.D2-0, U3.D2-3, LED4.green_cathode
  N16: U3.D3-0, U3.D3-3, LED4.blue_cathode
  N17: U3.D8-0, U3.D8-2, U3.D8-3, R8.Pin_1, S2.Pin_3, S2.Pin_4
  N18: U3.GND3-2, U3.GND8-0, R6.Pin_0, R7.leg1, R8.Pin_0
  N19: U3.A0, R7.wiper
  N20: U3.VUSB-0, R7.leg2, S2.Pin_1, S2.Pin_2
  N21: LED4.common_anode, R6.Pin_1

notes:
  Prueba 5:
  Función duty clycle
  Función triangle
  Prueba 6:
  LED RGB (Ánodo Común), potenciómetro y botón
  Prueba 6:
  LED RGB (Cátodo Común), potenciómetro y botón

custom parts:
  ESP8266 NodeMCU LoLin base: ESP8266 based NodeMCU Base
