# Fritzing sketch ESQUEMÁTICO (FZZ) (saved by Fritzing 0.9.4)
breadboards: 3

parts:
  U1 = ESP8266 NodeMCU LoLin base
  U2 = 74HC595 [package="DIP16 [THT]"]
  LED1 = LED - 3mm [color="Green (555nm)" package="3 mm [THT]"]
  R1 = Resistor [tolerance=±5% resistance=220 package=THT]
  LED2 = LED - 3mm [color="Green (555nm)" package="3 mm [THT]"]
  R2 = Resistor [tolerance=±5% resistance=220 package=THT]
  LED3 = LED - 3mm [color="Green (555nm)" package="3 mm [THT]"]
  R3 = Resistor [tolerance=±5% resistance=220 package=THT]
  LED4 = LED - 3mm [color="Green (555nm)" package="3 mm [THT]"]
  R4 = Resistor [tolerance=±5% resistance=220 package=THT]
  LED5 = LED - 3mm [color="Green (555nm)" package="3 mm [THT]"]
  R5 = Resistor [tolerance=±5% resistance=220 package=THT]
  LED6 = LED - 3mm [color="Green (555nm)" package="3 mm [THT]"]
  R6 = Resistor [tolerance=±5% resistance=220 package=THT]
  LED7 = LED - 3mm [color="Green (555nm)" package="3 mm [THT]"]
  R7 = Resistor [tolerance=±5% resistance=220 package=THT]
  LED8 = LED - 3mm [color="Green (555nm)" package="3 mm [THT]"]
  R8 = Resistor [tolerance=±5% resistance=220 package=THT]
  U3 = ESP8266 NodeMCU LoLin base
  U4 = 74HC595 [package="DIP16 [THT]"]
  R9 = Resistor [tolerance=±5% resistance=220 package=THT]
  R12 = Resistor [tolerance=±5% resistance=220 package=THT]
  7_Segment1 = 7 Segment Display
  S1 = Pushbutton [package="[THT]"]
  R13 = Resistor [tolerance=±5% resistance=10k package=THT]
  U5 = ESP8266 NodeMCU LoLin base
  U6 = 74HC595 [package="DIP16 [THT]"]
  R14 = Resistor [tolerance=±5% resistance=220 package=THT]
  R15 = Resistor [tolerance=±5% resistance=220 package=THT]
  7_Segment2 = 7 Segment Display
  S2 = Pushbutton [package="[THT]"]
  R16 = Resistor [tolerance=±5% resistance=10k package=THT]

nets:
  N1: U1.D0-0, U1.D0-3, U2.SH_CP
  N2: U1.D1-0, U1.D1-3, U2.ST_CP
  N3: U1.D2-0, U1.D2-3, U2.DS
  N4: U1.GND3-2, U1.GND8-0, U2.GND, U2.OE, R1.Pin_1, R2.Pin_1, R3.Pin_1, R4.Pin_1, R5.Pin_1, R6.Pin_1, R7.Pin_1, R8.Pin_1
  N5: U1.VUSB-0, U1.VUSB-1, U2.MR, U2.VCC
  N6: U2.Q1, LED2.anode
  N7: U2.Q2, LED3.anode
  N8: U2.Q3, LED4.anode
  N9: U2.Q4, LED5.anode
  N10: U2.Q5, LED6.anode
  N11: U2.Q6, LED7.anode
  N12: U2.Q7, LED8.anode
  N13: U2.Q0, LED1.anode
  N14: LED1.cathode, R1.Pin_0
  N15: LED2.cathode, R2.Pin_0
  N16: LED3.cathode, R3.Pin_0
  N17: LED4.cathode, R4.Pin_0
  N18: LED5.cathode, R5.Pin_0
  N19: LED6.cathode, R6.Pin_0
  N20: LED7.cathode, R7.Pin_0
  N21: LED8.cathode, R8.Pin_0
  N22: U3.D0-0, U3.D0-3, U4.SH_CP
  N23: U3.D1-0, U3.D1-3, U4.ST_CP
  N24: U3.D2-0, U3.D2-3, U4.DS
  N25: U3.D8-0, U3.D8-2, S1.Pin_3, S1.Pin_4, R13.Pin_0
  N26: U3.GND3-2, U3.GND8-0, U4.GND, U4.OE, R9.Pin_1, R12.Pin_0, R13.Pin_1
  N27: U3.VUSB-0, U3.VUSB-1, U4.MR, U4.VCC, S1.Pin_1, S1.Pin_2
  N28: U4.Q1, 7_Segment1.Segment_B
  N29: U4.Q2, 7_Segment1.Segment_C
  N30: U4.Q3, 7_Segment1.Segment_D
  N31: U4.Q4, 7_Segment1.Segment_E
  N32: U4.Q5, 7_Segment1.Segment_F
  N33: U4.Q6, 7_Segment1.Segment_G
  N34: U4.Q0, 7_Segment1.Segment_A
  N35: R9.Pin_0, R12.Pin_1, 7_Segment1.common_cathode
  N36: U5.D0-0, U5.D0-3, U6.SH_CP
  N37: U5.D1-0, U5.D1-3, U6.ST_CP
  N38: U5.D2-0, U5.D2-3, U6.DS
  N39: U5.D8-0, U5.D8-2, S2.Pin_3, S2.Pin_4, R16.Pin_0
  N40: U5.GND3-2, U5.GND8-0, U6.GND, U6.OE, R16.Pin_1
  N41: U5.VUSB-0, U6.MR, U6.VCC, R14.Pin_0, R15.Pin_1, S2.Pin_1, S2.Pin_2
  N42: U6.Q1, 7_Segment2.Segment_B
  N43: U6.Q2, 7_Segment2.Segment_C
  N44: U6.Q3, 7_Segment2.Segment_D
  N45: U6.Q4, 7_Segment2.Segment_E
  N46: U6.Q5, 7_Segment2.Segment_F
  N47: U6.Q6, 7_Segment2.Segment_G
  N48: U6.Q0, 7_Segment2.Segment_A
  N49: R14.Pin_1, R15.Pin_0, 7_Segment2.common_cathode

notes:
  Display Cátodo Común
  Display Ánodo Común

custom parts:
  ESP8266 NodeMCU LoLin base: ESP8266 based NodeMCU Base
