# Fritzing sketch ESQUEMÁTICO (FZZ) (saved by Fritzing 0.9.4)
breadboards: 2

parts:
  U1 = ESP8266 NodeMCU LoLin base
  7_Segment3 = 7 Segment Display
  S3 = Pushbutton [package="[THT]"]
  R17 = Resistor [tolerance=±5% resistance=10k package=THT]
  U2 = 74HC595 [package="DIP16 [THT]"]
  R18 = Resistor [tolerance=±5% resistance=220 package=THT]
  R19 = Resistor [tolerance=±5% resistance=220 package=THT]
  R20 = Resistor [tolerance=±5% resistance=220 package=THT]
  R21 = Resistor [tolerance=±5% resistance=220 package=THT]
  R22 = Resistor [tolerance=±5% resistance=220 package=THT]
  R23 = Resistor [tolerance=±5% resistance=220 package=THT]
  R24 = Resistor [tolerance=±5% resistance=220 package=THT]
  R25 = Resistor [tolerance=±5% resistance=220 package=THT]
  R26 = Resistor [tolerance=±5% resistance=220 package=THT]
  R27 = Resistor [tolerance=±5% resistance=220 package=THT]
  D1 = Rectifier Diode [part_number=1N4001 package="300 mil [THT]"]
  D2 = Rectifier Diode [part_number=1N4001 package="300 mil [THT]"]
  D3 = Rectifier Diode [part_number=1N4001 package="300 mil [THT]"]
  D4 = Rectifier Diode [part_number=1N4001 package="300 mil [THT]"]
  D5 = Rectifier Diode [part_number=1N4001 package="300 mil [THT]"]
  D6 = Rectifier Diode [part_number=1N4001 package="300 mil [THT]"]
  D7 = Rectifier Diode [part_number=1N4001 package="300 mil [THT]"]
  D8 = Rectifier Diode [part_number=1N4001 package="300 mil [THT]"]
  U3 = 74HC595 [package="DIP16 [THT]"]
  U4 = ESP8266 NodeMCU LoLin base
  7_Segment4 = 7 Segment Display
  S4 = Pushbutton [package="[THT]"]
  R28 = Resistor [tolerance=±5% resistance=10k package=THT]
  U5 = 74HC595 [package="DIP16 [THT]"]
  U6 = 74HC595 [package="DIP16 [THT]"]
  R29 = Resistor [tolerance=±5% resistance=220 package=THT]
  R30 = Resistor [tolerance=±5% resistance=220 package=THT]
  R31 = Resistor [tolerance=±5% resistance=220 package=THT]
  R32 = Resistor [tolerance=±5% resistance=220 package=THT]
  R33 = Resistor [tolerance=±5% resistance=220 package=THT]
  R34 = Resistor [tolerance=±5% resistance=220 package=THT]
  R35 = Resistor [tolerance=±5% resistance=220 package=THT]
  R36 = Resistor [tolerance=±5% resistance=220 package=THT]
  R37 = Resistor [tolerance=±5% resistance=220 package=THT]
  R38 = Resistor [tolerance=±5% resistance=220 package=THT]
  D9 = Rectifier Diode [part_number=1N4001 package="300 mil [THT]"]
  D10 = Rectifier Diode [part_number=1N4001 package="300 mil [THT]"]
  D11 = Rectifier Diode [part_number=1N4001 package="300 mil [THT]"]
  D12 = Rectifier Diode [part_number=1N4001 package="300 mil [THT]"]
  D13 = Rectifier Diode [part_number=1N4001 package="300 mil [THT]"]
  D14 = Rectifier Diode [part_number=1N4001 package="300 mil [THT]"]
  D15 = Rectifier Diode [part_number=1N4001 package="300 mil [THT]"]
  D16 = Rectifier Diode [part_number=1N4001 package="300 mil [THT]"]

nets:
  GND: U1.GND1-0, U1.D2-0, U1.D2-1, U1.D2-3, U1.GND3-2, U1.GND8-0, U1.GND8-9, U1.GND8-10, R17.Pin_1, U2.GND, U2.OE, U2.DS, R18.Pin_1, R19.Pin_1, R20.Pin_1, R21.Pin_1, R22.Pin_1, R23.Pin_1, R24.Pin_1, R25.Pin_1, R26.Pin_0, R27.Pin_1, U3.GND, U3.OE
  N1: U1.D0-0, U1.D0-1, U1.D0-3, U2.SH_CP, U3.SH_CP
  N2: U1.D1-0, U1.D1-1, U1.D1-3, U2.ST_CP, U3.ST_CP
  N3: U1.D7-0, U1.D7-2, U1.D7-3, U1.D8-0, U1.D8-2, S3.Pin_4, R17.Pin_0
  VCC: U1.VUSB-0, U1.VUSB-2, S3.Pin_2, U2.MR, U2.VCC, U3.MR, U3.VCC
  N4: 7_Segment3.Segment_E, U3.Q3
  N5: 7_Segment3.Segment_D, U3.Q2
  N6: 7_Segment3.common_cathode, R26.Pin_1, R27.Pin_0
  N7: 7_Segment3.Segment_C, U3.Q1
  N8: 7_Segment3.Segment_DP, U3.Q0
  N9: 7_Segment3.Segment_B, U3.Q7
  N10: 7_Segment3.Segment_A, U3.Q6
  N11: 7_Segment3.Segment_F, U3.Q5
  N12: 7_Segment3.Segment_G, U3.Q4
  N13: U2.Q1, D2.anode
  N14: U2.Q2, D3.anode
  N15: U2.Q3, D4.anode
  N16: U2.Q4, D5.anode
  N17: U2.Q5, D7.anode
  N18: U2.Q6, D8.anode
  N19: U2.Q7, D6.anode
  N20: U2.Q7', U3.DS
  N21: U2.Q0, D1.anode
  N22: R18.Pin_0, D1.cathode
  N23: R19.Pin_0, D2.cathode
  N24: R20.Pin_0, D3.cathode
  N25: R21.Pin_0, D4.cathode
  N26: R22.Pin_0, D5.cathode
  N27: R23.Pin_0, D7.cathode
  N28: R24.Pin_0, D8.cathode
  N29: R25.Pin_0, D6.cathode
  N30: U4.D0-0, U4.D0-1, U4.D0-3, U5.SH_CP, U6.SH_CP
  N31: U4.D1-0, U4.D1-1, U4.D1-3, U5.ST_CP, U6.ST_CP
  N32: U4.D2-0, U4.D2-1, U4.D2-3, U5.DS
  N33: U4.D7-0, U4.D7-2, U4.D7-3, U4.D8-0, U4.D8-2, S4.Pin_4, R28.Pin_0
  GND_2: U4.GND3-0, U4.GND8-0, U4.GND8-10, U4.GND8-11, R28.Pin_1, U5.GND, U5.OE, U6.GND, U6.OE, R29.Pin_1, R30.Pin_1, R32.Pin_1, R34.Pin_1, R35.Pin_1, R36.Pin_1, R37.Pin_1, R38.Pin_1
  VCC_2: U4.VUSB-0, S4.Pin_2, U5.MR, U5.VCC, U6.MR, U6.VCC, R31.Pin_0, R33.Pin_1
  N34: 7_Segment4.Segment_E, U6.Q3
  N35: 7_Segment4.Segment_D, U6.Q2
  N36: 7_Segment4.common_cathode, R31.Pin_1, R33.Pin_0
  N37: 7_Segment4.Segment_C, U6.Q1
  N38: 7_Segment4.Segment_DP, U6.Q0
  N39: 7_Segment4.Segment_B, U6.Q7
  N40: 7_Segment4.Segment_A, U6.Q6
  N41: 7_Segment4.Segment_F, U6.Q5
  N42: 7_Segment4.Segment_G, U6.Q4
  N43: U5.Q1, D10.anode
  N44: U5.Q2, D14.anode
  N45: U5.Q3, D12.anode
  N46: U5.Q4, D13.anode
  N47: U5.Q5, D15.anode
  N48: U5.Q6, D16.anode
  N49: U5.Q7, D11.anode
  N50: U5.Q7', U6.DS
  N51: U5.Q0, D9.anode
  N52: R29.Pin_0, D9.cathode
  N53: R30.Pin_0, D11.cathode
  N54: R32.Pin_0, D12.cathode
  N55: R34.Pin_0, D10.cathode
  N56: R35.Pin_0, D15.cathode
  N57: R36.Pin_0, D14.cathode
  N58: R37.Pin_0, D16.cathode
  N59: R38.Pin_0, D13.cathode

notes:
  Display Cátodo Común
  (Nota: sustituir diodos por LEDs)
  Display Ánodo Común
  (Nota: sustituir diodos por LEDs)

custom parts:
  ESP8266 NodeMCU LoLin base: ESP8266 based NodeMCU Base
