# Fritzing sketch ESQUEMÁTICO (FZZ) (saved by Fritzing 0.9.4)
breadboards: 1

parts:
  R1 = Resistor [tolerance=±5% resistance=220 package=THT]
  R2 = Resistor [tolerance=±5% resistance=220 package=THT]
  R3 = Resistor [tolerance=±5% resistance=220 package=THT]
  R4 = Resistor [tolerance=±5% resistance=220 package=THT]
  R5 = Resistor [tolerance=±5% resistance=220 package=THT]
  LED1 = LED - 3mm [color="Red (633nm)" package="3 mm [THT]"]
  LED2 = LED - 3mm [color="Red (633nm)" package="3 mm [THT]"]
  LED3 = LED - 3mm [color="Red (633nm)" package="3 mm [THT]"]
  LED4 = LED - 3mm [color="Red (633nm)" package="3 mm [THT]"]
  LED6 = LED - 3mm [color="Red (633nm)" package="3 mm [THT]"]
  U1 = ESP8266 NodeMCU LoLin base
  M1 = Dagu DGServo 9g (Top view) [part_number=RS001B]

nets:
  N1: R1.Pin_0, LED1.cathode
  N2: R1.Pin_1, R2.Pin_1, R3.Pin_1, R4.Pin_1, R5.Pin_1, U1.GND1-0, U1.GND8-0, U1.GND8-8, M1.gnd
  N3: R2.Pin_0, LED2.cathode
  N4: R3.Pin_0, LED4.cathode
  N5: R4.Pin_0, LED3.cathode
  N6: R5.Pin_0, LED6.cathode
  N7: LED1.anode, U1.D2-0, U1.D2-2
  N8: LED2.anode, U1.D3-0, U1.D3-2
  N9: LED3.anode, U1.D5-0, U1.D5-3
  N10: LED4.anode, U1.D4-0, U1.D4-2
  N11: LED6.anode, U1.D6-0, U1.D6-2
  N12: U1.D1-0, U1.D1-3, M1.pulse
  N13: U1.VUSB-0, M1.vcc

custom parts:
  ESP8266 NodeMCU LoLin base: ESP8266 based NodeMCU Base
