# Fritzing sketch ESQUEMÁTICO (FZZ) (saved by Fritzing 0.9.4)
breadboards: 1

parts:
  U1 = ESP8266 NodeMCU LoLin base
  R6 = Rotary Potentiometer (Large) [maximum_resistance=100kΩ package=THT]
  M1 = Dagu DGServo 9g (End View) [part_number=RS001B]
  R7 = Resistor [tolerance=±5% resistance=220 package=THT]
  D1 = Rectifier Diode [part_number=1N4001 package="300 mil [THT]"]
  U2 = 74HC595 [package="DIP16 [THT]"]
  R8 = Resistor [tolerance=±5% resistance=220 package=THT]
  D2 = Rectifier Diode [part_number=1N4001 package="300 mil [THT]"]
  R9 = Resistor [tolerance=±5% resistance=220 package=THT]
  R10 = Resistor [tolerance=±5% resistance=220 package=THT]
  D3 = Rectifier Diode [part_number=1N4001 package="300 mil [THT]"]
  D4 = Rectifier Diode [part_number=1N4001 package="300 mil [THT]"]
  R11 = Resistor [tolerance=±5% resistance=220 package=THT]
  R12 = Resistor [tolerance=±5% resistance=220 package=THT]
  D5 = Rectifier Diode [part_number=1N4001 package="300 mil [THT]"]
  D6 = Rectifier Diode [part_number=1N4001 package="300 mil [THT]"]
  R13 = Resistor [tolerance=±5% resistance=220 package=THT]
  R14 = Resistor [tolerance=±5% resistance=220 package=THT]
  D7 = Rectifier Diode [part_number=1N4001 package="300 mil [THT]"]
  D8 = Rectifier Diode [part_number=1N4001 package="300 mil [THT]"]

nets:
  N1: U1.D1-0, U1.D1-3, M1.pulse
  N2: U1.D2-0, U1.D2-2, U2.SH_CP
  N3: U1.D3-0, U1.D3-2, U2.ST_CP
  N4: U1.D4-0, U1.D4-2, U2.DS
  N5: U1.A0, R6.wiper
  VCC: U1.VUSB-0, U1.VUSB-3, R6.leg2, M1.vcc, U2.MR, U2.VCC
  GND: U1.GND8-0, U1.GND8-3, U1.GND8-4, R6.leg1, M1.gnd, R7.Pin_1, U2.GND, U2.OE, R8.Pin_1, R9.Pin_1, R10.Pin_1, R11.Pin_1, R12.Pin_1, R13.Pin_1, R14.Pin_1
  N6: R7.Pin_0, D1.cathode
  N7: D1.anode, U2.Q0
  N8: U2.Q1, D2.anode
  N9: U2.Q2, D3.anode
  N10: U2.Q3, D4.anode
  N11: U2.Q4, D5.anode
  N12: U2.Q5, D6.anode
  N13: U2.Q6, D7.anode
  N14: U2.Q7, D8.anode
  N15: R8.Pin_0, D2.cathode
  N16: R9.Pin_0, D3.cathode
  N17: R10.Pin_0, D4.cathode
  N18: R11.Pin_0, D5.cathode
  N19: R12.Pin_0, D6.cathode
  N20: R13.Pin_0, D7.cathode
  N21: R14.Pin_0, D8.cathode

custom parts:
  ESP8266 NodeMCU LoLin base: ESP8266 based NodeMCU Base
