# Fritzing sketch ESQUEMÁTICO (FZZ) (saved by Fritzing 0.9.4)
breadboards: 1

parts:
  KY-1 = Keyes Relay [package=THT]
  U1 = ESP8266 NodeMCU LoLin base
  R1 = Resistor [tolerance=±5% resistance=220 package=THT]
  R2 = Resistor [tolerance=±5% resistance=220 package=THT]
  LED1 = LED - 5mm [color="Red (633nm)" package="5 mm [THT]"]
  LED2 = LED - 5mm [color="Red (633nm)" package="5 mm [THT]"]
  S1 = Pushbutton [package="[THT]"]
  R3 = Resistor [tolerance=±5% resistance=10k package=THT]

nets:
  N1: KY-1.signal, U1.D0-0, U1.D0-2
  N2: KY-1.power, U1.VUSB-0, U1.VUSB-1, S1.Pin_1, S1.Pin_2
  N3: KY-1.ground, U1.GND3-2, U1.GND8-0, U1.GND8-1, R1.Pin_1, R2.Pin_1, R3.Pin_1
  N4: KY-1.NC, LED1.anode
  N5: KY-1.C, U1.3V1-0, U1.3V3-2
  N6: KY-1.NO, LED2.anode
  N7: U1.D8-0, S1.Pin_3, S1.Pin_4, R3.Pin_0
  N8: R1.Pin_0, LED1.cathode
  N9: R2.Pin_0, LED2.cathode

custom parts:
  Keyes Relay: The Keyes 5V relay module is suitable for SCM development, home appliance control. It uses a 5V~12V TIL control signal which can control DC / AC signal.
  ESP8266 NodeMCU LoLin base: ESP8266 based NodeMCU Base
