# Fritzing sketch ESQUEMÁTICO (FZZ) (saved by Fritzing 0.9.4)
breadboards: 1

parts:
  KY-1 = Keyes Relay [package=THT]
  U1 = ESP8266 NodeMCU LoLin base
  R1 = Resistor [tolerance=±5% resistance=220 package=THT]
  R2 = Resistor [tolerance=±5% resistance=220 package=THT]
  LED1 = LED - 5mm [color="Red (633nm)" package="5 mm [THT]"]
  LED2 = LED - 5mm [color="Red (633nm)" package="5 mm [THT]"]
  U2 = 74HC595 [package="DIP16 [THT]"]
  R3 = Rotary Potentiometer (Large) [maximum_resistance=100kΩ package=THT]
  R4 = Resistor [tolerance=±5% resistance=220 package=THT]
  R5 = Resistor [tolerance=±5% resistance=220 package=THT]
  D1 = Rectifier Diode [part_number=1N4001 package="300 mil [THT]"]
  D2 = Rectifier Diode [part_number=1N4001 package="300 mil [THT]"]
  R6 = Resistor [tolerance=±5% resistance=220 package=THT]
  R7 = Resistor [tolerance=±5% resistance=220 package=THT]
  D3 = Rectifier Diode [part_number=1N4001 package="300 mil [THT]"]
  D4 = Rectifier Diode [part_number=1N4001 package="300 mil [THT]"]
  R8 = Resistor [tolerance=±5% resistance=220 package=THT]
  R9 = Resistor [tolerance=±5% resistance=220 package=THT]
  D5 = Rectifier Diode [part_number=1N4001 package="300 mil [THT]"]
  D6 = Rectifier Diode [part_number=1N4001 package="300 mil [THT]"]
  R10 = Resistor [tolerance=±5% resistance=220 package=THT]
  R11 = Resistor [tolerance=±5% resistance=220 package=THT]
  D7 = Rectifier Diode [part_number=1N4001 package="300 mil [THT]"]
  D8 = Rectifier Diode [part_number=1N4001 package="300 mil [THT]"]

nets:
  N1: KY-1.signal, U1.D3-0, U1.D3-2, U1.D3-3, U1.D4-0, U1.D4-2
  N2: KY-1.power, U1.VUSB-0, U1.VUSB-1, U1.VUSB-3, U2.MR, U2.VCC, R3.leg2
  GND4: KY-1.ground, U1.GND3-2, U1.A0, U1.GND4, U1.GND8-0, U1.GND8-3, R1.Pin_1, R2.Pin_1, U2.GND, U2.OE, R3.leg1, R3.wiper, R4.Pin_1, R5.Pin_1, R6.Pin_1, R7.Pin_1, R8.Pin_1, R9.Pin_1, R10.Pin_1, R11.Pin_1
  N3: KY-1.NC, LED1.anode
  N4: KY-1.C, U1.3V3-0, U1.3V3-2
  N5: KY-1.NO, LED2.anode
  N6: U1.D0-0, U1.D0-3, U2.SH_CP
  N7: U1.D1-0, U1.D1-3, U2.ST_CP
  N8: U1.D2-0, U1.D2-3, U2.DS
  N9: R1.Pin_0, LED1.cathode
  N10: R2.Pin_0, LED2.cathode
  N11: U2.Q1, D2.anode
  N12: U2.Q2, D3.anode
  N13: U2.Q3, D4.anode
  N14: U2.Q4, D5.anode
  N15: U2.Q5, D6.anode
  N16: U2.Q6, D7.anode
  N17: U2.Q7, D8.anode
  N18: U2.Q0, D1.anode
  N19: R4.Pin_0, D1.cathode
  N20: R5.Pin_0, D2.cathode
  N21: R6.Pin_0, D4.cathode
  N22: R7.Pin_0, D3.cathode
  N23: R8.Pin_0, D6.cathode
  N24: R9.Pin_0, D5.cathode
  N25: R10.Pin_0, D8.cathode
  N26: R11.Pin_0, D7.cathode

custom parts:
  Keyes Relay: The Keyes 5V relay module is suitable for SCM development, home appliance control. It uses a 5V~12V TIL control signal which can control DC / AC signal.
  ESP8266 NodeMCU LoLin base: ESP8266 based NodeMCU Base
