# Fritzing sketch ESQUEMÁTICO (FZZ) (saved by Fritzing 0.9.4)
breadboards: 1

parts:
  LCD1 = LCD screen
  R1 = Rotary Potentiometer (Large) [maximum_resistance=100kΩ package=THT]
  R2 = Resistor [tolerance=±5% resistance=220 package=THT]
  LED1 = LED - 5mm [color="Red (633nm)" package="5 mm [THT]"]
  R3 = Resistor [tolerance=±5% resistance=220 package=THT]
  LED2 = LED - 5mm [color="Red (633nm)" package="5 mm [THT]"]
  S1 = Pushbutton [package="[THT]"]
  R4 = Resistor [tolerance=±5% resistance=10k package=THT]
  U1 = ESP8266 NodeMCU LoLin base

nets:
  N1: LCD1.VSS, LCD1.R/W, LCD1.LED-, R1.leg1, R2.Pin_1, R3.Pin_1, R4.Pin_1, U1.GND1-0, U1.GND3-3, U1.GND8-11
  N2: LCD1.VDD, LCD1.LED+, R1.leg2, S1.Pin_3, S1.Pin_4, U1.VUSB-0
  N3: LCD1.V0, R1.wiper
  N4: LCD1.RS, U1.D0-0, U1.D0-3
  N5: LCD1.E, U1.D1-0, U1.D1-3
  N6: LCD1.DB4, U1.D2-0, U1.D2-3
  N7: LCD1.DB5, U1.D3-0, U1.D3-3
  N8: LCD1.DB6, U1.D4-0, U1.D4-3
  N9: LCD1.DB7, U1.D5-0, U1.D5-3
  N10: R2.Pin_0, LED1.anode
  N11: LED1.cathode, U1.D6-0, U1.D6-2
  N12: R3.Pin_0, LED2.anode
  N13: LED2.cathode, U1.D7-0
  N14: S1.Pin_1, S1.Pin_2, R4.Pin_0, U1.D8-0, U1.D8-3

custom parts:
  ESP8266 NodeMCU LoLin base: ESP8266 based NodeMCU Base
